# Fritzing sketch 3LED (saved by Fritzing 0.9.2b)
breadboards: 1

parts:
  Raspberry_Pi_2 = Raspberry Pi 2
  LED1 = LED - 5mm [color="Red (660nm)" package="5 mm [THT]"]
  R1 = Resistor [tolerance=±5% resistance=330 package=THT]
  R2 = Resistor [tolerance=±5% resistance=330 package=THT]
  LED2 = LED - 5mm [color="Yellow (595nm)" package="5 mm [THT]"]
  R3 = Resistor [tolerance=±5% resistance=330 package=THT]
  LED3 = LED - 5mm [color="Green (555nm)" package="5 mm [THT]"]

nets:
  N1: Raspberry_Pi_2.GPIO21, R3.Pin_0
  N2: Raspberry_Pi_2.GPIO20, R2.Pin_0
  N3: Raspberry_Pi_2.GPIO16, R1.Pin_0
  N4: Raspberry_Pi_2.GND, LED1.cathode, LED2.cathode, LED3.cathode
  N5: LED1.anode, R1.Pin_1
  N6: R2.Pin_1, LED2.anode
  N7: R3.Pin_1, LED3.anode
